// Logisim project RISC-V single cycle processor .circ as structural Verilog: 7 circuits, main circuit main
module main (
  input  in_1
);

  wire and_1_out, bit_extender_1_out, clock_1_out, controller_1_out_2, controller_1_out_3,
       controller_1_out_4, controller_1_out_5, controller_1_out_6, controller_1_out_7, controller_1_out_8,
       controller_1_out_9, controller_1_out_10, controller_1_u, imm_generator_1_out_9, or_1_out, or_2_out;
  wire [3:0] rom_1_data_2;
  wire [7:0] alu_1_out_6_2;
  wire [23:0] alu_1_out_6;
  wire [31:0] adder_1_out, imm_generator_1_out_6, imm_generator_1_out_7, imm_generator_1_out_8,
       imm_generator_1_sb, multiplexer_1_out, multiplexer_2_out, multiplexer_3_out, multiplexer_4_out,
       multiplexer_5_out, multiplexer_6_out, multiplexer_7_out, ram_1_data, reg_file_1_out_10,
       reg_file_1_out_11, register_1_q, rom_1_data;

  Multiplexer #(.width(32), .enable("false")) multiplexer_1 (
    .in0(adder_1_out), .in1({alu_1_out_6_2, alu_1_out_6}), .out(multiplexer_1_out), .sel(controller_1_out_9));
  Multiplexer #(.width(32), .enable("false")) multiplexer_2 (
    .in0(multiplexer_1_out), .in1(imm_generator_1_out_8), .out(multiplexer_2_out), .sel(controller_1_out_8));
  Multiplexer #(.width(32), .enable("false")) multiplexer_3 (
    .in0(multiplexer_2_out), .in1(imm_generator_1_sb), .out(multiplexer_3_out), .sel(and_1_out));
  Clock clock_1 (.out(clock_1_out));
  Register #(.width(32)) register_1 (
    .D(multiplexer_3_out), .Q(register_1_q), .clk(clock_1_out), .clr(in_1));  // open: en
  Adder #(.width(32)) adder_1 (.a(32'h4), .b(register_1_q), .out(adder_1_out));  // open: cin, cout
  or or_1 (or_1_out, controller_1_out_8, controller_1_out_9);
  Multiplexer #(.width(32), .enable("false")) multiplexer_4 (
    .in0(multiplexer_7_out), .in1(adder_1_out), .out(multiplexer_4_out), .sel(or_1_out));
  ROM #(.addrWidth(24), .dataWidth(32)) rom_1 (
    .addr(register_1_q[25:2]),
    .data({rom_1_data[31], rom_1_data_2[3], rom_1_data[29:15], rom_1_data_2[2:0], rom_1_data[11:0]}));  // open: sel
  Multiplexer #(.width(32), .enable("false")) multiplexer_5 (
    .in0(multiplexer_4_out), .in1(imm_generator_1_out_7), .out(multiplexer_5_out), .sel(controller_1_u));
  IMM_Generator imm_generator_1 (
    .in_1({rom_1_data[31], rom_1_data_2[3], rom_1_data[29:15], rom_1_data_2[2:0], rom_1_data[11:0]}),
    .SB(imm_generator_1_sb), .out_7(imm_generator_1_out_7), .out_8(imm_generator_1_out_8),
    .out_6(imm_generator_1_out_6), .out_9(imm_generator_1_out_9), .in_2(register_1_q));  // open: out_3, out_4
  Controller controller_1 (
    .in_1(rom_1_data[6:0]), .out_2(controller_1_out_2), .out_3(controller_1_out_3),
    .out_4(controller_1_out_4), .out_5(controller_1_out_5), .out_6(controller_1_out_6),
    .out_7(controller_1_out_7), .out_8(controller_1_out_8), .out_9(controller_1_out_9),
    .out_10(controller_1_out_10), .U(controller_1_u));
  Reg_File reg_file_1 (
    .in_1(in_1), .in_3(multiplexer_5_out), .Rd(rom_1_data[11:7]), .Rs2(rom_1_data[24:20]),
    .in_9(controller_1_out_5), .out_11(reg_file_1_out_11), .in_2(clock_1_out), .out_10(reg_file_1_out_10),
    .in_4(controller_1_out_4), .Rs1(rom_1_data[19:15]), .in_6(controller_1_out_3));
  Multiplexer #(.width(32), .enable("false")) multiplexer_6 (
    .in0(reg_file_1_out_11), .in1(imm_generator_1_out_6), .out(multiplexer_6_out), .sel(imm_generator_1_out_9));
  Multiplexer #(.width(32), .enable("false")) multiplexer_7 (
    .in0({alu_1_out_6_2, alu_1_out_6}), .in1(ram_1_data), .out(multiplexer_7_out), .sel(controller_1_out_6));
  Alu alu_1 (
    .in_1(reg_file_1_out_10), .in_2(multiplexer_6_out), .in_5(rom_1_data_2),
    .out_6({alu_1_out_6_2, alu_1_out_6}), .in_4(controller_1_out_7), .in_3(controller_1_out_10));
  Bit_Extender #(.in_width(32), .out_width(1)) bit_extender_1 (
    .in({alu_1_out_6_2, alu_1_out_6}), .out(bit_extender_1_out));
  or or_2 (or_2_out, controller_1_out_2, controller_1_out_6);
  and and_1 (and_1_out, controller_1_out_7, bit_extender_1_out);
  RAM #(.addrWidth(24), .dataWidth(32), .bus("separate")) ram_1 (
    .addr(alu_1_out_6), .din(reg_file_1_out_11), .data(ram_1_data), .str(controller_1_out_2), .sel(or_2_out),
    .clk(clock_1_out), .ld(controller_1_out_6), .clr(in_1));

  // Notes on the sheet:
  //   Faizan Saeed
  //   contents of rom_1 (hex, n*v repeats v):
  //   1100f13 1e02023 693 613 593 100593 2783 60533 168693 b50633 fed780e3 16f713 fe0706e3 605b3 fe9ff0ef
endmodule

module Alu (
  input  [31:0] in_1,
  input  [31:0] in_2,
  input  in_3,
  input  in_4,
  input  [3:0] in_5,
  output [31:0] out_6
);

  wire comparator_1_eq, comparator_2_eq, comparator_2_gt, comparator_3_eq, comparator_3_gt, comparator_4_lt,
       comparator_5_lt, comparator_6_eq, not_1_out, or_2_out, or_3_out;
  wire [3:0] bit_extender_7_out, multiplexer_8_out;
  wire [31:0] adder_1_out, and_1_out, bit_extender_1_out, bit_extender_2_out, bit_extender_3_out,
       bit_extender_4_out, bit_extender_5_out, bit_extender_6_out, multiplexer_1_out, multiplexer_2_out,
       multiplexer_3_out, multiplexer_4_out, multiplexer_5_out, multiplexer_6_out, or_1_out, shifter_1_out,
       shifter_2_out, subtractor_1_out, xor_1_out;

  Adder #(.width(32)) adder_1 (.a(in_1), .b(in_2), .out(adder_1_out));  // open: cin, cout
  Subtractor #(.width(32)) subtractor_1 (.a(in_1), .b(in_2), .out(subtractor_1_out));  // open: bin, bout
  assign and_1_out = in_1 & in_2;  // AND_Gate and_1, 32 bits wide
  assign or_1_out = in_1 | in_2;  // OR_Gate or_1, 32 bits wide
  Shifter #(.width(32)) shifter_1 (.in(in_2), .\dist (in_1[4:0]), .out(shifter_1_out));
  Shifter #(.width(32), .shift("lr")) shifter_2 (.in(in_1), .\dist (in_2[4:0]), .out(shifter_2_out));
  assign xor_1_out = in_1 ^ in_2;  // XOR_Gate xor_1, 32 bits wide
  Comparator #(.width(32)) comparator_1 (.a(in_1), .b(in_2), .eq(comparator_1_eq));  // open: gt, lt
  Comparator #(.width(32)) comparator_2 (.a(in_1), .b(in_2), .gt(comparator_2_gt), .eq(comparator_2_eq));  // open: lt
  Comparator #(.width(32), .mode("unsigned")) comparator_3 (
    .a(in_1), .b(in_2), .gt(comparator_3_gt), .eq(comparator_3_eq));  // open: lt
  Comparator #(.width(32)) comparator_4 (.a(in_1), .b(in_2), .lt(comparator_4_lt));  // open: gt, eq
  Comparator #(.width(32), .mode("unsigned")) comparator_5 (.a(in_1), .b(in_2), .lt(comparator_5_lt));  // open: gt, eq
  Comparator #(.width(32)) comparator_6 (.a(in_1), .b(in_2), .eq(comparator_6_eq));  // open: gt, lt
  Multiplexer #(.width(32), .enable("false")) multiplexer_1 (
    .in0(adder_1_out), .in1(bit_extender_1_out), .out(multiplexer_1_out), .sel(in_4));
  Multiplexer #(.width(32), .enable("false")) multiplexer_2 (
    .in0(and_1_out), .in1(bit_extender_3_out), .out(multiplexer_2_out), .sel(in_4));
  Multiplexer #(.width(32), .enable("false")) multiplexer_3 (
    .in0(or_1_out), .in1(bit_extender_5_out), .out(multiplexer_3_out), .sel(in_4));
  Multiplexer #(.width(32), .enable("false")) multiplexer_4 (
    .in0(shifter_1_out), .in1(bit_extender_6_out), .out(multiplexer_4_out), .sel(in_4));
  Multiplexer #(.width(32), .enable("false")) multiplexer_5 (
    .in0(shifter_2_out), .in1(bit_extender_2_out), .out(multiplexer_5_out), .sel(in_4));
  Multiplexer #(.width(32), .enable("false")) multiplexer_6 (
    .in0(xor_1_out), .in1(bit_extender_4_out), .out(multiplexer_6_out), .sel(in_4));
  not not_1 (not_1_out, comparator_6_eq);
  assign bit_extender_1_out = {{31{1'b0}}, comparator_1_eq};  // Bit_Extender bit_extender_1
  or or_2 (or_2_out, comparator_2_gt, comparator_2_eq);
  assign bit_extender_2_out = {{31{1'b0}}, or_2_out};  // Bit_Extender bit_extender_2
  assign bit_extender_3_out = {{31{1'b0}}, or_3_out};  // Bit_Extender bit_extender_3
  or or_3 (or_3_out, comparator_3_gt, comparator_3_eq);
  assign bit_extender_4_out = {{31{1'b0}}, comparator_4_lt};  // Bit_Extender bit_extender_4
  assign bit_extender_5_out = {{31{1'b0}}, comparator_5_lt};  // Bit_Extender bit_extender_5
  assign bit_extender_6_out = {{31{1'b0}}, not_1_out};  // Bit_Extender bit_extender_6
  Multiplexer #(.select(4), .width(32), .disabled(0), .enable("false")) multiplexer_7 (
    .in0(multiplexer_1_out), .in1(multiplexer_4_out), .in2(adder_1_out), .in4(multiplexer_6_out),
    .in5(multiplexer_5_out), .in6(multiplexer_3_out), .in7(multiplexer_2_out), .in8(subtractor_1_out),
    .out(out_6), .sel(multiplexer_8_out));  // open: in3, in9, in10, in11, in12, in13, in14, in15
  Multiplexer #(.width(4), .enable("false")) multiplexer_8 (
    .in0(bit_extender_7_out), .in1(in_5), .out(multiplexer_8_out), .sel(in_3));
  assign bit_extender_7_out = {{1{1'b0}}, in_5[2:0]};  // Bit_Extender bit_extender_7
endmodule

module Reg_File (
  input  in_1,
  input  in_2,
  input  [31:0] in_3,
  input  in_4,
  input  [4:0] Rs1,
  input  in_6,
  input  [4:0] Rd,
  input  [4:0] Rs2,
  input  in_9,
  output [31:0] out_10,
  output [31:0] out_11
);

  wire demultiplexer_1_out0, demultiplexer_1_out1, demultiplexer_1_out2, demultiplexer_1_out3,
       demultiplexer_1_out4, demultiplexer_1_out5, demultiplexer_1_out6, demultiplexer_1_out7,
       demultiplexer_1_out8, demultiplexer_1_out9, demultiplexer_1_out10, demultiplexer_1_out11,
       demultiplexer_1_out12, demultiplexer_1_out13, demultiplexer_1_out14, demultiplexer_1_out15,
       demultiplexer_1_out16, demultiplexer_1_out17, demultiplexer_1_out18, demultiplexer_1_out19,
       demultiplexer_1_out20, demultiplexer_1_out21, demultiplexer_1_out22, demultiplexer_1_out23,
       demultiplexer_1_out24, demultiplexer_1_out25, demultiplexer_1_out26, demultiplexer_1_out27,
       demultiplexer_1_out28, demultiplexer_1_out29, demultiplexer_1_out30, demultiplexer_1_out31;
  wire [31:0] and_1_out, register_1_q, register_2_q, register_3_q, register_4_q, register_5_q, register_6_q,
       register_7_q, register_8_q, register_9_q, register_10_q, register_11_q, register_12_q, register_13_q,
       register_14_q, register_15_q, register_16_q, register_17_q, register_18_q, register_19_q,
       register_20_q, register_21_q, register_22_q, register_23_q, register_24_q, register_25_q,
       register_26_q, register_27_q, register_28_q, register_29_q, register_30_q, register_31_q,
       register_32_q;

  Demultiplexer #(.select(5), .enable("false")) demultiplexer_1 (
    .out0(demultiplexer_1_out0), .out1(demultiplexer_1_out1), .out2(demultiplexer_1_out2),
    .out3(demultiplexer_1_out3), .out4(demultiplexer_1_out4), .out5(demultiplexer_1_out5),
    .out6(demultiplexer_1_out6), .out7(demultiplexer_1_out7), .out8(demultiplexer_1_out8),
    .out9(demultiplexer_1_out9), .out10(demultiplexer_1_out10), .out11(demultiplexer_1_out11),
    .out12(demultiplexer_1_out12), .out13(demultiplexer_1_out13), .out14(demultiplexer_1_out14),
    .out15(demultiplexer_1_out15), .out16(demultiplexer_1_out16), .out17(demultiplexer_1_out17),
    .out18(demultiplexer_1_out18), .out19(demultiplexer_1_out19), .out20(demultiplexer_1_out20),
    .out21(demultiplexer_1_out21), .out22(demultiplexer_1_out22), .out23(demultiplexer_1_out23),
    .out24(demultiplexer_1_out24), .out25(demultiplexer_1_out25), .out26(demultiplexer_1_out26),
    .out27(demultiplexer_1_out27), .out28(demultiplexer_1_out28), .out29(demultiplexer_1_out29),
    .out30(demultiplexer_1_out30), .out31(demultiplexer_1_out31), .in(in_6), .sel(Rd));
  assign and_1_out = {32{1'b0}};  // AND_Gate and_1, 32 bits wide AND_Gate
  Register #(.width(32)) register_1 (
    .D(and_1_out), .en(demultiplexer_1_out0), .Q(register_1_q), .clk(in_2), .clr(in_1));
  Register #(.width(32)) register_2 (.D(in_3), .en(demultiplexer_1_out1), .Q(register_2_q), .clk(in_2), .clr(in_1));
  Register #(.width(32)) register_3 (.D(in_3), .en(demultiplexer_1_out2), .Q(register_3_q), .clk(in_2), .clr(in_1));
  Register #(.width(32)) register_4 (.D(in_3), .en(demultiplexer_1_out3), .Q(register_4_q), .clk(in_2), .clr(in_1));
  Register #(.width(32)) register_5 (.D(in_3), .en(demultiplexer_1_out4), .Q(register_5_q), .clk(in_2), .clr(in_1));
  Register #(.width(32)) register_6 (.D(in_3), .en(demultiplexer_1_out5), .Q(register_6_q), .clk(in_2), .clr(in_1));
  Register #(.width(32)) register_7 (.D(in_3), .en(demultiplexer_1_out6), .Q(register_7_q), .clk(in_2), .clr(in_1));
  Register #(.width(32)) register_8 (.D(in_3), .en(demultiplexer_1_out7), .Q(register_8_q), .clk(in_2), .clr(in_1));
  Register #(.width(32)) register_9 (.D(in_3), .en(demultiplexer_1_out8), .Q(register_9_q), .clk(in_2), .clr(in_1));
  Register #(.width(32)) register_10 (.D(in_3), .en(demultiplexer_1_out9), .Q(register_10_q), .clk(in_2), .clr(in_1));
  Register #(.width(32)) register_11 (.D(in_3), .en(demultiplexer_1_out10), .Q(register_11_q), .clk(in_2), .clr(in_1));
  Register #(.width(32)) register_12 (.D(in_3), .en(demultiplexer_1_out11), .Q(register_12_q), .clk(in_2), .clr(in_1));
  Register #(.width(32)) register_13 (.D(in_3), .en(demultiplexer_1_out12), .Q(register_13_q), .clk(in_2), .clr(in_1));
  Register #(.width(32)) register_14 (.D(in_3), .en(demultiplexer_1_out13), .Q(register_14_q), .clk(in_2), .clr(in_1));
  Register #(.width(32)) register_15 (.D(in_3), .en(demultiplexer_1_out14), .Q(register_15_q), .clk(in_2), .clr(in_1));
  Register #(.width(32)) register_16 (.D(in_3), .en(demultiplexer_1_out15), .Q(register_16_q), .clk(in_2), .clr(in_1));
  Register #(.width(32)) register_17 (.D(in_3), .en(demultiplexer_1_out16), .Q(register_17_q), .clk(in_2), .clr(in_1));
  Register #(.width(32)) register_18 (.D(in_3), .en(demultiplexer_1_out17), .Q(register_18_q), .clk(in_2), .clr(in_1));
  Register #(.width(32)) register_19 (.D(in_3), .en(demultiplexer_1_out18), .Q(register_19_q), .clk(in_2), .clr(in_1));
  Register #(.width(32)) register_20 (.D(in_3), .en(demultiplexer_1_out19), .Q(register_20_q), .clk(in_2), .clr(in_1));
  Register #(.width(32)) register_21 (.D(in_3), .en(demultiplexer_1_out20), .Q(register_21_q), .clk(in_2), .clr(in_1));
  Register #(.width(32)) register_22 (.D(in_3), .en(demultiplexer_1_out21), .Q(register_22_q), .clk(in_2), .clr(in_1));
  Register #(.width(32)) register_23 (.D(in_3), .en(demultiplexer_1_out22), .Q(register_23_q), .clk(in_2), .clr(in_1));
  Register #(.width(32)) register_24 (.D(in_3), .en(demultiplexer_1_out23), .Q(register_24_q), .clk(in_2), .clr(in_1));
  Register #(.width(32)) register_25 (.D(in_3), .en(demultiplexer_1_out24), .Q(register_25_q), .clk(in_2), .clr(in_1));
  Register #(.width(32)) register_26 (.D(in_3), .en(demultiplexer_1_out25), .Q(register_26_q), .clk(in_2), .clr(in_1));
  Register #(.width(32)) register_27 (.D(in_3), .en(demultiplexer_1_out26), .Q(register_27_q), .clk(in_2), .clr(in_1));
  Register #(.width(32)) register_28 (.D(in_3), .en(demultiplexer_1_out27), .Q(register_28_q), .clk(in_2), .clr(in_1));
  Register #(.width(32)) register_29 (.D(in_3), .en(demultiplexer_1_out28), .Q(register_29_q), .clk(in_2), .clr(in_1));
  Register #(.width(32)) register_30 (.D(in_3), .en(demultiplexer_1_out29), .Q(register_30_q), .clk(in_2), .clr(in_1));
  Register #(.width(32)) register_31 (.D(in_3), .en(demultiplexer_1_out30), .Q(register_31_q), .clk(in_2), .clr(in_1));
  Register #(.width(32)) register_32 (
    .D(in_3), .en(demultiplexer_1_out31), .Q(register_32_q), .clk(in_2));  // open: clr
  Multiplexer #(.select(5), .width(32)) multiplexer_1 (
    .in0(register_1_q), .in1(register_2_q), .in2(register_3_q), .in3(register_4_q), .in4(register_5_q),
    .in5(register_6_q), .in6(register_7_q), .in7(register_8_q), .in8(register_9_q), .in9(register_10_q),
    .in10(register_11_q), .in11(register_12_q), .in12(register_13_q), .in13(register_14_q),
    .in14(register_15_q), .in15(register_16_q), .in16(register_17_q), .in17(register_18_q),
    .in18(register_19_q), .in19(register_20_q), .in20(register_21_q), .in21(register_22_q),
    .in22(register_23_q), .in23(register_24_q), .in24(register_25_q), .in25(register_26_q),
    .in26(register_27_q), .in27(register_28_q), .in28(register_29_q), .in29(register_30_q),
    .in30(register_31_q), .in31(register_32_q), .out(out_10), .sel(Rs1), .en(in_4));
  Multiplexer #(.select(5), .width(32)) multiplexer_2 (
    .in0(register_1_q), .in1(register_2_q), .in2(register_3_q), .in3(register_4_q), .in4(register_5_q),
    .in5(register_6_q), .in6(register_7_q), .in7(register_8_q), .in8(register_9_q), .in9(register_10_q),
    .in10(register_11_q), .in11(register_12_q), .in12(register_13_q), .in13(register_14_q),
    .in14(register_15_q), .in15(register_16_q), .in16(register_17_q), .in17(register_18_q),
    .in18(register_19_q), .in19(register_20_q), .in20(register_21_q), .in21(register_22_q),
    .in22(register_23_q), .in23(register_24_q), .in24(register_25_q), .in25(register_26_q),
    .in26(register_27_q), .in27(register_28_q), .in28(register_29_q), .in29(register_30_q),
    .in30(register_31_q), .in31(register_32_q), .out(out_11), .sel(Rs2), .en(in_9));

  // Notes on the sheet:
  //   Rd Data
  //   Rs1 Data
  //   Rs2 Data
endmodule

module IMM_Generator (
  input  [31:0] in_1,
  input  [31:0] in_2,
  output [31:0] out_3,
  output [31:0] out_4,
  output [31:0] SB,
  output [31:0] out_6,
  output [31:0] out_7,
  output [31:0] out_8,
  output out_9
);

  wire type_decoder_1_auipc, type_decoder_1_i_type, type_decoder_1_jalr, type_decoder_1_load;
  wire [1:0] or_1_out;
  wire [31:0] adder_3_out, bit_extender_2_out, bit_extender_3_out;

  Type_Decoder type_decoder_1 (
    .in_1(in_1[6:0]), .I_Type(type_decoder_1_i_type), .S_Type(or_1_out[1]), .Load(type_decoder_1_load),
    .Jalr(type_decoder_1_jalr), .auipc(type_decoder_1_auipc));  // open: R_Type, SB_Type, U_Type, UJ_Type, OP4
  assign out_3 = {{20{in_1[31]}}, in_1[31:20]};  // Bit_Extender bit_extender_1
  or or_1 (or_1_out[0], type_decoder_1_load, type_decoder_1_i_type, type_decoder_1_jalr);
  assign bit_extender_2_out = {{19{in_1[31]}}, {in_1[31], in_1[7], in_1[30:25], in_1[11:8], 1'b0}};  // Bit_Extender bit_extender_2
  Adder #(.width(32)) adder_1 (.a(bit_extender_2_out), .b(in_2), .out(SB));  // open: cin, cout
  assign bit_extender_3_out = {{11{in_1[31]}}, {in_1[31], in_1[19:12], in_1[20], in_1[30:21], 1'b0}};  // Bit_Extender bit_extender_3
  Adder #(.width(32)) adder_2 (.a(bit_extender_3_out), .b(in_2), .out(out_8));  // open: cin, cout
  assign out_4 = {{20{in_1[31]}}, {in_1[31:25], in_1[11:7]}};  // Bit_Extender bit_extender_4
  Adder #(.width(32)) adder_3 (.a({in_1[31:12], {12{1'b0}}}), .b(in_2), .out(adder_3_out));  // open: cin, cout
  Multiplexer #(.width(32), .enable("false")) multiplexer_1 (
    .in0({in_1[31:12], {12{1'b0}}}), .in1(adder_3_out), .out(out_7), .sel(type_decoder_1_auipc));
  or or_2 (out_9, or_1_out[0], or_1_out[1]);
  Multiplexer #(.select(2), .width(32), .enable("false")) multiplexer_2 (
    .in1(out_3), .in2(out_4), .out(out_6), .sel(or_1_out));  // open: in0, in3

  // Notes on the sheet:
  //   I
  //   S
  //   UJ
  //   U
endmodule

module Controller (
  input  [6:0] in_1,
  output out_2,
  output out_3,
  output out_4,
  output out_5,
  output out_6,
  output out_7,
  output out_8,
  output out_9,
  output out_10,
  output U
);

  wire type_decoder_1_i_type, type_decoder_1_jalr, type_decoder_1_load, type_decoder_1_r_type,
       type_decoder_1_s_type, type_decoder_1_sb_type, type_decoder_1_uj_type;

  Type_Decoder type_decoder_1 (
    .in_1(in_1), .R_Type(type_decoder_1_r_type), .I_Type(type_decoder_1_i_type),
    .S_Type(type_decoder_1_s_type), .SB_Type(type_decoder_1_sb_type), .U_Type(U),
    .UJ_Type(type_decoder_1_uj_type), .Load(type_decoder_1_load), .Jalr(type_decoder_1_jalr), .OP4(out_10));  // open: auipc
  Cont cont_1 (
    .MemWrite(out_2), .R(type_decoder_1_r_type), .I(type_decoder_1_i_type), .S(type_decoder_1_s_type),
    .SB(type_decoder_1_sb_type), .U(U), .UJ(type_decoder_1_uj_type), .Rd_En(out_3), .Rs1_En(out_4),
    .Rs2_En(out_5), .Load(type_decoder_1_load), .Mem_Read(out_6), .Branch(out_7), .UJ_2(out_8),
    .Jalr(type_decoder_1_jalr), .Jalr_2(out_9));
endmodule

module Type_Decoder (
  input  [6:0] in_1,
  output OP4,
  output R_Type,
  output Load,
  output I_Type,
  output Jalr,
  output S_Type,
  output SB_Type,
  output U_Type,
  output UJ_Type,
  output auipc
);

  wire comparator_1_eq, comparator_5_eq, comparator_8_eq, comparator_9_eq, comparator_11_eq;

  Comparator #(.width(7)) comparator_1 (.a(7'b0110011), .b(in_1), .eq(comparator_1_eq));  // open: gt, lt
  Comparator #(.width(7)) comparator_2 (.a(7'b0000011), .b(in_1), .eq(Load));  // open: gt, lt
  Comparator #(.width(7)) comparator_3 (.a(7'b0100011), .b(in_1), .eq(S_Type));  // open: gt, lt
  Comparator #(.width(7)) comparator_4 (.a(7'b1100011), .b(in_1), .eq(SB_Type));  // open: gt, lt
  Comparator #(.width(7)) comparator_5 (.a(7'b0110111), .b(in_1), .eq(comparator_5_eq));  // open: gt, lt
  Comparator #(.width(7)) comparator_6 (.a(7'b1101111), .b(in_1), .eq(UJ_Type));  // open: gt, lt
  Comparator #(.width(7)) comparator_7 (.a(7'b0010111), .b(in_1), .eq(auipc));  // open: gt, lt
  Comparator #(.width(7)) comparator_8 (.a(7'b0111011), .b(in_1), .eq(comparator_8_eq));  // open: gt, lt
  Comparator #(.width(7)) comparator_9 (.a(7'b0011011), .b(in_1), .eq(comparator_9_eq));  // open: gt, lt
  Comparator #(.width(7)) comparator_10 (.a(7'b1100111), .b(in_1), .eq(Jalr));  // open: gt, lt
  or or_1 (R_Type, comparator_1_eq, comparator_8_eq);
  Comparator #(.width(7)) comparator_11 (.a(7'b0010011), .b(in_1), .eq(comparator_11_eq));  // open: gt, lt
  or or_2 (U_Type, comparator_5_eq, auipc);
  or or_3 (OP4, comparator_9_eq, comparator_11_eq, R_Type);
  or or_4 (I_Type, comparator_9_eq, comparator_11_eq);
endmodule

module Cont (
  input  Jalr,
  input  Load,
  input  R,
  input  I,
  input  S,
  input  SB,
  input  U,
  input  UJ,
  output Rd_En,
  output MemWrite,
  output Rs1_En,
  output Rs2_En,
  output Mem_Read,
  output Branch,
  output UJ_2,
  output Jalr_2
);

  or or_1 (Rd_En, R, I, Load, UJ, U);
  or or_2 (Rs1_En, SB, S, I, R);
  or or_3 (Rs2_En, R, S, SB);

  assign Branch = SB;
  assign Jalr_2 = Jalr;
  assign Mem_Read = Load;
  assign MemWrite = S;
  assign UJ_2 = UJ;
endmodule
